# Fritzing sketch PCB_Layout (saved by Fritzing 0.9.6b)
perfboards: 1

parts:
  MH-ET_LIVE_ESP32_DEVKIT1 = MH-ET LIVE ESP32 DEVKIT 38 pins
  Bauteil1 = Analog Digital MUX Breakout
  Bauteil2 = Analog Digital MUX Breakout
  J1 = female pin header, 19 pins [form="♀ (female)"]
  J2 = female pin header, 19 pins [form="♀ (female)"]
  J3 = male pin header, 16 pins [form="♂ (male)"]
  J4 = male pin header, 16 pins [form="♂ (male)"]
  J5 = male pin header, 8 pins [form="♂ (male)"]
  J6 = male pin header, 8 pins [form="♂ (male)"]
  J7 = screw terminal, 4 pins
  J8 = screw terminal, 3 pins
  J9 = screw terminal, 3 pins
  J10 = screw terminal, 3 pins
  J11 = screw terminal, 3 pins
  J12 = screw terminal, 3 pins
  J13 = screw terminal, 3 pins
  J14 = screw terminal, 3 pins
  J15 = screw terminal, 3 pins  # not connected
  J16 = screw terminal, 3 pins
  J17 = screw terminal, 3 pins
  J18 = screw terminal, 3 pins  # not connected
  J19 = screw terminal, 3 pins  # not connected
  J20 = screw terminal, 3 pins  # not connected
  J21 = screw terminal, 3 pins  # not connected
  J22 = screw terminal, 3 pins  # not connected
  J23 = screw terminal, 3 pins
  J24 = screw terminal, 4 pins
  J25 = screw terminal, 4 pins  # not connected
  J26 = screw terminal, 4 pins  # not connected
  J27 = screw terminal, 4 pins  # not connected
  J28 = Screw terminal - 2 pins [package=THT]
  J29 = Screw terminal - 2 pins [package=THT]
  OLED1 = OLED 128x64 I2C Monochrome Display
  S1 = Pushbutton [package="[THT]"]
  R1 = Resistor [tolerance=±5% resistance=10k package=THT]
  Capacitive_Soil_Moisture_Sensor1 = DFRobot Capacitive Soil Moisture Sensor V1.0 [part_number=SEN0193]
  U1 = Module 4 Relais 5V [package="Module 4 Relais 5V"]

nets:
  N1: MH-ET_LIVE_ESP32_DEVKIT1.3V3, J1.pin19, J8.pin2
  N2: MH-ET_LIVE_ESP32_DEVKIT1.RST, J1.pin18
  N3: MH-ET_LIVE_ESP32_DEVKIT1.SVP, Bauteil2.SIG, J1.pin17, J5.pin8
  N4: MH-ET_LIVE_ESP32_DEVKIT1.SVN, J1.pin16, S1.Pin_3, S1.Pin_4, R1.Pin_0
  N5: MH-ET_LIVE_ESP32_DEVKIT1.IO34, J1.pin15
  N6: MH-ET_LIVE_ESP32_DEVKIT1.IO35, J1.pin14
  N7: MH-ET_LIVE_ESP32_DEVKIT1.IO32, J1.pin13
  N8: MH-ET_LIVE_ESP32_DEVKIT1.IO33, J1.pin12
  N9: MH-ET_LIVE_ESP32_DEVKIT1.IO25, J1.pin11
  N10: MH-ET_LIVE_ESP32_DEVKIT1.IO26, J1.pin10
  N11: MH-ET_LIVE_ESP32_DEVKIT1.IO27, J1.pin9
  N12: MH-ET_LIVE_ESP32_DEVKIT1.IO14, J1.pin8, J7.pin4, OLED1.SDA
  N13: MH-ET_LIVE_ESP32_DEVKIT1.IO12, J1.pin7, J7.pin3, OLED1.SCK
  N14: MH-ET_LIVE_ESP32_DEVKIT1.GND#58, Bauteil2.GND, J1.pin6, J5.pin1, J8.pin1, J12.pin1, J13.pin1, J29.pin1
  N15: MH-ET_LIVE_ESP32_DEVKIT1.IO13, J1.pin5
  N16: MH-ET_LIVE_ESP32_DEVKIT1.SD2, J1.pin4
  N17: MH-ET_LIVE_ESP32_DEVKIT1.SD3, J1.pin3
  N18: MH-ET_LIVE_ESP32_DEVKIT1.CMD, J1.pin2
  VCC: MH-ET_LIVE_ESP32_DEVKIT1.5V, Bauteil2.VCC, J1.pin1, J5.pin2, J7.pin2, J28.pin2, J29.pin2, OLED1.VDD, U1.VCC
  N19: MH-ET_LIVE_ESP32_DEVKIT1.GND#64, J2.pin19
  N20: MH-ET_LIVE_ESP32_DEVKIT1.IO23, Bauteil2.S3, J2.pin18, J5.pin7
  N21: MH-ET_LIVE_ESP32_DEVKIT1.IO22, Bauteil2.S2, J2.pin17, J5.pin6
  N22: MH-ET_LIVE_ESP32_DEVKIT1.TXD0, Bauteil2.S1, J2.pin16, J5.pin5
  N23: MH-ET_LIVE_ESP32_DEVKIT1.RXD0, Bauteil2.S0, J2.pin15, J5.pin4
  N24: MH-ET_LIVE_ESP32_DEVKIT1.IO21, J2.pin14
  N25: MH-ET_LIVE_ESP32_DEVKIT1.GND#70, J2.pin13
  N26: MH-ET_LIVE_ESP32_DEVKIT1.IO19, J2.pin12
  N27: MH-ET_LIVE_ESP32_DEVKIT1.IO18, J2.pin11
  N28: MH-ET_LIVE_ESP32_DEVKIT1.IO5, J2.pin10
  N29: MH-ET_LIVE_ESP32_DEVKIT1.IO17, J2.pin9
  N30: MH-ET_LIVE_ESP32_DEVKIT1.IO16, J2.pin8
  N31: MH-ET_LIVE_ESP32_DEVKIT1.IO4, J2.pin7
  N32: MH-ET_LIVE_ESP32_DEVKIT1.IO0, J2.pin6
  N33: MH-ET_LIVE_ESP32_DEVKIT1.IO2, J2.pin5
  N34: MH-ET_LIVE_ESP32_DEVKIT1.IO15, J2.pin4
  N35: MH-ET_LIVE_ESP32_DEVKIT1.SD1, J2.pin3
  N36: MH-ET_LIVE_ESP32_DEVKIT1.SD0, J2.pin2
  N37: MH-ET_LIVE_ESP32_DEVKIT1.SCK, J2.pin1
  N38: Bauteil1.C0, J3.pin16
  N39: Bauteil1.C1, J3.pin15
  N40: Bauteil1.C2, J3.pin14
  N41: Bauteil1.C3, J3.pin13
  N42: Bauteil1.C4, J3.pin12
  N43: Bauteil1.C5, J3.pin11
  N44: Bauteil1.C6, J3.pin10
  N45: Bauteil1.C7, J3.pin9
  N46: Bauteil1.C8, J3.pin8
  N47: Bauteil1.C9, J3.pin7
  N48: Bauteil1.C10, J3.pin6
  N49: Bauteil1.C11, J3.pin5
  N50: Bauteil1.C12, J3.pin4
  N51: Bauteil1.C13, J3.pin3
  N52: Bauteil1.C14, J3.pin2
  N53: Bauteil1.C15, J3.pin1
  N54: Bauteil1.GND, J6.pin8
  N55: Bauteil1.VCC, J6.pin7
  N56: Bauteil1.EN, J6.pin6
  N57: Bauteil1.S0, J6.pin5
  N58: Bauteil1.S1, J6.pin4
  N59: Bauteil1.S2, J6.pin3
  N60: Bauteil1.S3, J6.pin2
  N61: Bauteil1.SIG, J6.pin1
  N62: Bauteil2.C0, J4.pin1
  N63: Bauteil2.C1, J4.pin2
  N64: Bauteil2.C2, J4.pin3, J14.pin3
  N65: Bauteil2.C3, J4.pin4, J12.pin3
  N66: Bauteil2.C4, J4.pin5, J10.pin3
  N67: Bauteil2.C5, J4.pin6, J11.pin3
  N68: Bauteil2.C6, J4.pin7, J9.pin3, Capacitive_Soil_Moisture_Sensor1.A
  N69: Bauteil2.C7, J4.pin8, J8.pin3
  N70: Bauteil2.C8, J4.pin9
  N71: Bauteil2.C9, J4.pin10
  N72: Bauteil2.C10, J4.pin11
  N73: Bauteil2.C11, J4.pin12
  N74: Bauteil2.C12, J4.pin13
  N75: Bauteil2.C13, J4.pin14
  N76: Bauteil2.C14, J4.pin15
  N77: Bauteil2.C15, J4.pin16
  N78: Bauteil2.EN, J5.pin3
  GND: J7.pin1, J28.pin1, OLED1.GND, U1.GND
  N79: J9.pin1, Capacitive_Soil_Moisture_Sensor1.GND
  N80: J9.pin2, J17.pin2, Capacitive_Soil_Moisture_Sensor1.VCC
  N81: J16.pin2, J23.pin2
  N82: J24.pin1, U1.IN1
  N83: J24.pin2, U1.IN2
  N84: J24.pin3, U1.IN3
  N85: J24.pin4, U1.IN4
  N86: S1.Pin_1, S1.Pin_2

custom parts:
  MH-ET LIVE ESP32 DEVKIT 38 pins: http://mh.nodebb.com/topic/2/mh-et-live-esp32-devkit
  DFRobot Capacitive Soil Moisture Sensor V1.0: DFRobot Capacitive Soil Moisture Sensor V1.0 This product measures soil moisture levels by capacitive sensing, rather than resistive sensing like other types of moisture sensor. It is made of a corrosion resistant material giving it a long service life. Insert it into soil and impress your friends with the real-time soil moisture data! The product includes an on-board voltage regulator which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
  Module 4 Relais 5V: Module 4 Relais 5V 4x SPD-06VDC-SD-C
